// Logisim project WorkingSlaveOFHSG.circ as structural Verilog: 6 circuits, main circuit slave_fsm
// slave
module main (
  input  [7:0] datain,
  input  [1:0] addr,
  input  R_W,
  input  ready_M,
  input  valid,
  input  clk,
  input  clr,
  output [7:0] dataOut,
  output ready
);

  wire and_1_out, and_2_out, decoder_1_out0, decoder_1_out1, decoder_1_out2, decoder_1_out3, not_1_out;
  wire [7:0] register_1_q, register_2_q, register_3_q, register_4_q;

  slave_fsm slave_fsm (.valid(valid), .clk(clk), .ready(ready));  // open: q0, q1
  Decoder #(.select(2)) decoder_1 (
    .out0(decoder_1_out0), .out1(decoder_1_out1), .out2(decoder_1_out2), .out3(decoder_1_out3), .sel(addr),
    .en(and_1_out));
  and and_1 (and_1_out, R_W, ready, valid);
  Register register_1 (.D(datain), .en(decoder_1_out0), .Q(register_1_q), .clk(clk), .clr(clr));
  Register register_2 (.D(datain), .en(decoder_1_out1), .Q(register_2_q), .clk(clk), .clr(clr));
  Register register_3 (.D(datain), .en(decoder_1_out2), .Q(register_3_q), .clk(clk), .clr(clr));
  Register register_4 (.D(datain), .en(decoder_1_out3), .Q(register_4_q), .clk(clk), .clr(clr));
  Multiplexer #(.select(2), .width(8)) multiplexer_1 (
    .in0(register_1_q), .in1(register_2_q), .in2(register_3_q), .in3(register_4_q), .out(dataOut),
    .sel(addr), .en(and_2_out));
  and and_2 (and_2_out, not_1_out, ready_M);
  not not_1 (not_1_out, and_1_out);

  // Notes on the sheet:
  //   0 = read
  //   1 = write
endmodule

module slave_fsm (
  input  valid,
  input  clk,
  output q0,
  output q1,
  output ready
);

  wire and_1_out, and_2_out, or_1_out;

  and and_1 (and_1_out, ~q0, ~q1, valid);  // AND_Gate
  D_Flip_Flop d_ff_1 (.clk(clk), .D(and_1_out), .Q(q0));  // open: Qn, preset, en, reset
  and and_2 (and_2_out, ~q1, valid);  // AND_Gate
  or or_1 (or_1_out, and_2_out, q0);
  D_Flip_Flop d_ff_2 (.clk(clk), .D(or_1_out), .Q(q1));  // open: Qn, preset, en, reset
  and and_3 (ready, q1, ~q0);  // AND_Gate
endmodule

module bridge (
  input  PCLK,
  input  PRESETn,
  input  PSEL,
  input  PENABLE,
  input  [1:0] PADDR,
  input  [7:0] PWDATA,
  input  PWRITE,
  input  READY_M,
  input  [7:0] DATA_OUT,
  output CLK,
  output clr,
  output out_12,
  output [1:0] address,
  output [7:0] data,
  output R_W,
  output PREADY
);

  Register datasave (.D(DATA_OUT));  // open: en, Q, clk, clr
  not not_1 (clr, PRESETn);
  and and_1 (out_12, PSEL, PENABLE);

  assign address = PADDR;
  assign CLK = PCLK;
  assign data = PWDATA;
  assign PREADY = READY_M;
  assign R_W = PWRITE;

  // Notes on the sheet:
  //   ignore
endmodule

module ALOO (
  input  [1:0] address,
  input  [7:0] sendingData,
  input  R_W,
  input  pclk,
  input  in_5,
  output [1:0] out_6
);

  wire and_1_out, and_2_out, main_1_p7, not_1_out, shift_register_1_q0, shift_register_1_q1,
       shift_register_1_q2, shift_register_1_q3, shift_register_1_q4, shift_register_1_q5,
       shift_register_1_q6, shift_register_1_q7, shift_register_1_q8, shift_register_1_q9,
       shift_register_1_q10, shift_register_2_q2;
  wire [1:0] shift_register_2_q1;
  wire [7:0] main_1_p8, multiplexer_1_out, shift_register_2_q10;

  Clock clock_1 ();  // open: out
  Button control ();  // open: out
  slave_fsm slave_fsm_1 (.valid(in_5), .q0(out_6[0]), .q1(out_6[1]));  // open: clk, ready
  and and_1 (and_1_out, out_6[1], ~out_6[0]);  // AND_Gate
  Shift_Register #(.length(16)) shift_register_1 (
    .shift(1'b0), .clk(main_1_p7), .load(and_1_out), .d0(address[1]), .q0(shift_register_1_q0),
    .d1(address[0]), .q1(shift_register_1_q1), .d2(R_W), .q2(shift_register_1_q2), .d3(sendingData[7]),
    .q3(shift_register_1_q3), .d4(sendingData[6]), .q4(shift_register_1_q4), .d5(sendingData[5]),
    .q5(shift_register_1_q5), .d6(sendingData[4]), .q6(shift_register_1_q6), .d7(sendingData[3]),
    .q7(shift_register_1_q7), .d8(sendingData[2]), .q8(shift_register_1_q8), .d9(sendingData[1]),
    .q9(shift_register_1_q9), .d10(sendingData[0]), .q10(shift_register_1_q10));  // open: in, out, clr, d11, q11, d12, q12, d13, q13, d14, q14, d15, q15
  and and_2 (and_2_out, out_6[1], out_6[0]);
  Shift_Register #(.length(16)) shift_register_2 (
    .shift(1'b0), .clk(main_1_p7), .load(and_2_out), .d0(shift_register_1_q0), .q0(shift_register_2_q1[1]),
    .d1(shift_register_1_q1), .q1(shift_register_2_q1[0]), .d2(shift_register_1_q2),
    .q2(shift_register_2_q2), .d3(shift_register_1_q3), .q3(shift_register_2_q10[7]),
    .d4(shift_register_1_q4), .q4(shift_register_2_q10[6]), .d5(shift_register_1_q5),
    .q5(shift_register_2_q10[5]), .d6(shift_register_1_q6), .q6(shift_register_2_q10[4]),
    .d7(shift_register_1_q7), .q7(shift_register_2_q10[3]), .d8(shift_register_1_q8),
    .q8(shift_register_2_q10[2]), .d9(shift_register_1_q9), .q9(shift_register_2_q10[1]),
    .d10(shift_register_1_q10), .q10(shift_register_2_q10[0]));  // open: in, out, clr, d11, q11, d12, q12, d13, q13, d14, q14, d15, q15
  Multiplexer #(.width(8), .enable("false")) multiplexer_1 (
    .in1(shift_register_2_q10), .out(multiplexer_1_out), .sel(shift_register_2_q2));  // open: in0
  // main main_1: pin names not known; wires that end beside it: multiplexer_1_out, shift_register_2_q1, shift_register_2_q2, out_6[1], out_6[0], R_W, main_1_p7, main_1_p8
  Register register_1 (.D(main_1_p8), .en(not_1_out), .clk(main_1_p7), .clr(main_1_p7));  // open: Q
  not not_1 (not_1_out, shift_register_2_q2);

  // Notes on the sheet:
  //   Ignore
endmodule

module mains (
  input  [7:0] dataIn,
  input  [1:0] addr,
  input  W,
  input  masterReady,
  output [7:0] out_5
);

  wire clock_out, clr_out, main_1_ready, master_fsm_1_valid;

  Clock clock (.out(clock_out));
  Button clr (.out(clr_out));
  master_fsm master_fsm_1 (.clk(clock_out), .ready(main_1_ready), .valid(master_fsm_1_valid));
  main main_1 (
    .datain(dataIn), .addr(addr), .R_W(W), .ready_M(masterReady), .valid(master_fsm_1_valid),
    .clk(clock_out), .clr(clr_out), .dataOut(out_5), .ready(main_1_ready));
endmodule

// masterFsm
module master_fsm (
  input  clk,
  input  ready,
  output valid
);

  wire and_1_out, and_2_out, d_ff_1_q, d_ff_2_q, or_2_out;

  and and_1 (and_1_out, ~d_ff_2_q, ~d_ff_1_q, ready);  // AND_Gate
  D_Flip_Flop d_ff_1 (.clk(clk), .D(and_1_out), .Q(d_ff_1_q));  // open: Qn, preset, en, reset
  and and_2 (and_2_out, d_ff_2_q, ~ready);  // AND_Gate
  or or_1 (valid, d_ff_1_q, d_ff_2_q);
  or or_2 (or_2_out, and_2_out, d_ff_1_q);
  D_Flip_Flop d_ff_2 (.clk(clk), .D(or_2_out), .Q(d_ff_2_q));  // open: Qn, preset, en, reset
endmodule
